// Logisim project A 4-bit Bitwise Not Circuit.circ as structural Verilog: 1 circuit, main circuit main
module main (
  input  [3:0] \input ,
  output [3:0] \output 
);

  not not_1 (\output [0], \input [0]);
  not not_2 (\output [1], \input [1]);
  not not_3 (\output [2], \input [2]);
  not not_4 (\output [3], \input [3]);

  // Notes on the sheet:
  //   inverter
endmodule
