// Logisim project 1. One Bit Half Adder.circ as structural Verilog: 1 circuit, main circuit main
module main (
  input  A,
  input  B,
  output Sum,
  output Cout
);

  and and_1 (Cout, B, A);
  xor xor_1 (Sum, A, B);
endmodule
