// Logisim project 2. One Bit Full Adder.circ as structural Verilog: 1 circuit, main circuit main
module main (
  input  Cin,
  input  A,
  input  B,
  output Sum,
  output Cout
);

  wire and_2_out, and_3_out, and_out, xor_1_out;

  and \and  (and_out, B, A);
  and and_2 (and_2_out, B, Cin);
  and and_3 (and_3_out, A, Cin);
  xor xor_1 (xor_1_out, A, B);
  xor xor_2 (Sum, xor_1_out, Cin);
  or or_1 (Cout, and_3_out, and_2_out, and_out);
endmodule
