// Logisim project 2a. Full Adder - 2 bit.circ as structural Verilog: 1 circuit, main circuit main
module main (
  input  Cin,
  input  A0,
  input  A1,
  input  B0,
  input  B1,
  output Sum_0,
  output Sum_1,
  output Cout
);

  wire and_2_out, and_3_out, and_4_out, and_5_out, and_6_out, and_out, or_1_out, xor_1_out, xor_2_out;

  and \and  (and_out, A1, A0);
  and and_2 (and_2_out, B1, B0);
  and and_3 (and_3_out, A0, Cin);
  and and_4 (and_4_out, A1, Cin);
  or or_1 (or_1_out, and_out, and_4_out, and_3_out);
  and and_5 (and_5_out, B1, or_1_out);
  and and_6 (and_6_out, B0, or_1_out);
  or or_2 (Cout, and_2_out, and_5_out, and_6_out);
  xor xor_1 (xor_1_out, A0, A1);
  xor xor_2 (xor_2_out, B0, B1);
  xor xor_3 (Sum_0, xor_1_out, Cin);
  xor xor_4 (Sum_1, or_1_out, xor_2_out);
endmodule
