// Logisim project 3. 4-bit Adder.circ as structural Verilog: 1 circuit, main circuit main
module main (
  input  Cin,
  input  [3:0] A,
  input  [3:0] B,
  output [3:0] Sum,
  output Cout
);

  wire and_2_out, and_3_out, and_4_out, and_5_out, and_6_out, and_7_out, and_8_out, and_9_out, and_10_out,
       and_11_out, and_12_out, and_out, or_1_out, or_2_out, or_3_out, xor_1_out, xor_4_out, xor_5_out,
       xor_6_out;

  and \and  (and_out, B[0], Cin);
  and and_2 (and_2_out, B[0], A[0]);
  or or_1 (or_1_out, and_2_out, and_out, and_5_out);
  and and_3 (and_3_out, B[1], A[1]);
  and and_4 (and_4_out, B[1], or_1_out);
  or or_2 (or_2_out, and_3_out, and_4_out, and_6_out);
  and and_5 (and_5_out, A[0], Cin);
  and and_6 (and_6_out, A[1], or_1_out);
  xor xor_1 (xor_1_out, A[0], B[0]);
  xor xor_2 (Sum[0], xor_1_out, Cin);
  xor xor_3 (Sum[1], or_1_out, xor_4_out);
  xor xor_4 (xor_4_out, A[1], B[1]);
  and and_7 (and_7_out, B[2], A[2]);
  and and_8 (and_8_out, B[3], A[3]);
  and and_9 (and_9_out, B[2], or_2_out);
  and and_10 (and_10_out, A[2], or_2_out);
  or or_3 (or_3_out, and_7_out, and_9_out, and_10_out);
  and and_11 (and_11_out, A[3], or_3_out);
  and and_12 (and_12_out, B[3], or_3_out);
  or or_4 (Cout, and_8_out, and_12_out, and_11_out);
  xor xor_5 (xor_5_out, A[2], B[2]);
  xor xor_6 (xor_6_out, A[3], B[3]);
  xor xor_7 (Sum[2], xor_5_out, or_2_out);
  xor xor_8 (Sum[3], or_3_out, xor_6_out);
endmodule
