// Logisim project 4. Logisim 4-bit Adder.circ as structural Verilog: 1 circuit, main circuit main
module main (
  input  [3:0] A,
  input  Cin,
  input  [3:0] B,
  output Cout,
  output [3:0] Sum
);

  Adder #(.width(4)) adder_1 (.a(A), .b(B), .out(Sum), .cin(Cin), .cout(Cout));
endmodule
