// Logisim project 2. Multiplexer 1.circ as structural Verilog: 1 circuit, main circuit main
module main (
  input  [3:0] in_1,
  input  [3:0] in_2,
  input  in_3
);

  wire and_1_out, and_2_out, and_3_out, and_4_out, and_5_out, and_6_out, and_7_out, and_8_out, not_1_out,
       or_1_out, or_2_out, or_3_out, or_4_out;

  not not_1 (not_1_out, in_3);
  and and_1 (and_1_out, not_1_out, in_1[3]);
  and and_2 (and_2_out, not_1_out, in_1[1]);
  and and_3 (and_3_out, not_1_out, in_1[2]);
  or or_1 (or_1_out, and_1_out, and_5_out);
  LED led_1 (.in(or_1_out));
  and and_4 (and_4_out, not_1_out, in_1[0]);
  or or_2 (or_2_out, and_3_out, and_6_out);
  LED led_2 (.in(or_2_out));
  and and_5 (and_5_out, in_3, in_2[3]);
  or or_3 (or_3_out, and_2_out, and_7_out);
  LED led_3 (.in(or_3_out));
  and and_6 (and_6_out, in_3, in_2[2]);
  and and_7 (and_7_out, in_3, in_2[1]);
  or or_4 (or_4_out, and_4_out, and_8_out);
  LED led_4 (.in(or_4_out));
  and and_8 (and_8_out, in_3, in_2[0]);
endmodule
