// Logisim project 2. Multiplexer 2.circ as structural Verilog: 1 circuit, main circuit main
module main (
  input  [3:0] in_1,
  input  in_2,
  input  [3:0] in_3
);

  wire [3:0] multiplexer_1_out;

  Multiplexer #(.width(4), .enable("false")) multiplexer_1 (
    .in0(in_1), .in1(in_3), .out(multiplexer_1_out), .sel(in_2));
  LED led_1 (.in(multiplexer_1_out[0]));
  LED led_2 (.in(multiplexer_1_out[1]));
  LED led_3 (.in(multiplexer_1_out[2]));
  LED led_4 (.in(multiplexer_1_out[3]));
endmodule
