// Logisim project Part 1 - Adder-Subtracter.circ as structural Verilog: 1 circuit, main circuit main
module main (
  input  Su,
  input  [4:0] A,
  input  [4:0] B,
  output [4:0] Sum,
  output out_5
);

  wire [4:0] xor_1_out;

  xor xor_1 (xor_1_out[0], B[0], Su);
  xor xor_2 (xor_1_out[1], B[1], Su);
  xor xor_3 (xor_1_out[2], B[2], Su);
  xor xor_4 (xor_1_out[3], B[3], Su);
  xor xor_5 (xor_1_out[4], B[4], Su);
  Adder #(.width(5)) adder_1 (.a(A), .b(xor_1_out), .out(Sum), .cin(Su), .cout(out_5));
endmodule
