// Logisim project Part 2 - Two-Port Adder(with feedback).circ as structural Verilog: 1 circuit, main circuit main
module main (
  input  [1:0] Dmux,
  input  [1:0] Rmux,
  input  Sub
);

  wire clock_1_out, decoder_1_out0, decoder_1_out1, decoder_1_out2, decoder_1_out3;
  wire [7:0] adder_1_out, multiplexer_1_out, multiplexer_2_out, register_1_q, register_2_q, register_3_q,
       register_4_q, xor_1_out;

  Clock clock_1 (.out(clock_1_out));
  Register register_1 (.D(adder_1_out), .en(decoder_1_out0), .Q(register_1_q), .clr(clock_1_out));  // open: clk
  Register register_2 (.D(adder_1_out), .en(decoder_1_out1), .Q(register_2_q), .clr(clock_1_out));  // open: clk
  Register register_3 (.D(adder_1_out), .en(decoder_1_out2), .Q(register_3_q), .clr(clock_1_out));  // open: clk
  Register register_4 (.D(adder_1_out), .en(decoder_1_out3), .Q(register_4_q), .clr(clock_1_out));  // open: clk
  Decoder #(.select(2), .enable("false")) decoder_1 (
    .out0(decoder_1_out0), .out1(decoder_1_out1), .out2(decoder_1_out2), .out3(decoder_1_out3), .sel(Dmux));
  Multiplexer #(.select(2), .width(8), .enable("false")) multiplexer_1 (
    .in0(register_1_q), .in1(register_2_q), .in2(register_3_q), .in3(register_4_q), .out(multiplexer_1_out),
    .sel(Dmux));
  Multiplexer #(.select(2), .width(8), .enable("false")) multiplexer_2 (
    .in0(register_1_q), .in1(register_2_q), .in2(register_3_q), .in3(register_4_q), .out(multiplexer_2_out),
    .sel(Rmux));
  Adder adder_1 (.a(multiplexer_1_out), .b(xor_1_out), .out(adder_1_out), .cin(Sub));  // open: cout
  assign xor_1_out = multiplexer_2_out ^ {8{Sub}};  // XOR_Gate xor_1, 8 bits wide

  // Notes on the sheet:
  //   A reg
  //   B reg
  //   C reg
  //   D reg
endmodule
