// Logisim project Part 2 - Two-Port Adder.circ as structural Verilog: 1 circuit, main circuit main
module main (
  input  [4:0] in_1,
  input  [4:0] in_2,
  input  [4:0] in_3,
  input  [4:0] in_4,
  input  [1:0] Dmux,
  input  [1:0] Rmux,
  input  Sub,
  output [4:0] out_8
);

  wire [4:0] multiplexer_1_out, multiplexer_2_out, xor_1_out;

  Multiplexer #(.select(2), .width(5), .enable("false")) multiplexer_1 (
    .in0(in_1), .in1(in_2), .in2(in_3), .in3(in_4), .out(multiplexer_1_out), .sel(Dmux));
  Multiplexer #(.select(2), .width(5), .enable("false")) multiplexer_2 (
    .in0(in_1), .in1(in_2), .in2(in_3), .in3(in_4), .out(multiplexer_2_out), .sel(Rmux));
  assign xor_1_out = multiplexer_2_out ^ {5{Sub}};  // XOR_Gate xor_1, 5 bits wide
  Adder #(.width(5)) adder_1 (.a(multiplexer_1_out), .b(xor_1_out), .out(out_8), .cin(Sub));  // open: cout
endmodule
