// Logisim project SAM Datapath.circ as structural Verilog: 1 circuit, main circuit main
module main (
  input  Pc,
  input  InC,
  input  Amux,
  input  Mar,
  input  Mst,
  input  Ir,
  input  Dmux,
  input  Acc,
  input  Out,
  input  Sub,
  output [7:0] Output_Display
);

  wire and_1_out, clock_1_out, Clr_out, nand_1_out;
  wire [3:0] counter_1_q, multiplexer_1_out, not_1_out, register_1_q, register_2_q;
  wire [7:0] adder_1_out, multiplexer_2_out, ram_1_data, register_3_q, xor_1_out;
  wire [7:4] register_2_q_2;

  Clock clock_1 (.out(clock_1_out));
  Button Clr (.out(Clr_out));
  and and_1 (and_1_out, clock_1_out, nand_1_out);
  Counter #(.width(4), .max('hf)) counter_1 (
    .load(Pc), .D(register_2_q), .count(InC), .Q(counter_1_q), .clk(and_1_out), .clr(Clr_out));  // open: carry
  Multiplexer #(.width(4), .enable("false")) multiplexer_1 (
    .in0(counter_1_q), .in1(register_2_q), .out(multiplexer_1_out), .sel(Amux));
  Register #(.width(4)) register_1 (.D(multiplexer_1_out), .en(Mar), .Q(register_1_q), .clk(and_1_out));  // open: clr
  RAM #(.addrWidth(4), .bus("separate")) ram_1 (
    .addr(register_1_q), .din(register_3_q), .data(ram_1_data), .str(Mst), .clk(and_1_out));  // open: sel, ld, clr
  Multiplexer #(.width(8), .enable("false")) multiplexer_2 (
    .in0(adder_1_out), .in1(ram_1_data), .out(multiplexer_2_out), .sel(Dmux));
  Register register_2 (.D(ram_1_data), .en(Ir), .Q({register_2_q_2, register_2_q}), .clk(and_1_out), .clr(Clr_out));
  Register register_3 (.D(multiplexer_2_out), .en(Acc), .Q(register_3_q), .clk(and_1_out));  // open: clr
  nand nand_1 (nand_1_out, register_2_q_2[7], register_2_q_2[6], register_2_q_2[5], register_2_q_2[4]);
  Register register_4 (.D(register_3_q), .en(Out), .Q(Output_Display), .clk(and_1_out));  // open: clr
  assign xor_1_out = ram_1_data ^ {8{Sub}};  // XOR_Gate xor_1, 8 bits wide
  assign not_1_out = ~register_2_q_2;  // NOT_Gate not_1, 4 bits wide
  Adder adder_1 (.a(register_3_q), .b(xor_1_out), .out(adder_1_out), .cin(Sub));  // open: cout

  // Notes on the sheet:
  //   PC
  //   MAR
  //   IR
  //   ACC
  //   Hlt
  //   OUT
endmodule
