// Logisim project SAM Datapath with Control Logic.circ as structural Verilog: 1 circuit, main circuit main
module main (
  output [7:0] Output_Display,
  output Pc,
  output InC,
  output Amux,
  output Mar,
  output Mst,
  output Ir,
  output Dmux,
  output Acc,
  output Out,
  output Sub
);

  wire and_1_out, and_4_out, and_10_out, and_11_out, and_12_out, and_13_out, and_14_out, and_15_out,
       and_16_out, and_17_out, and_18_out, clock_1_out, Clr_out, decoder_1_out2, decoder_1_out3, nand_1_out,
       not_1_out, or_2_out, or_3_out, or_4_out;
  wire [1:0] counter_2_q;
  wire [3:0] counter_1_q, multiplexer_1_out, not_2_out, register_1_q, register_2_q;
  wire [7:0] adder_1_out, multiplexer_2_out, not_3_out, ram_1_data, register_3_q, xor_1_out;
  wire [7:4] register_2_q_2;

  Clock clock_1 (.out(clock_1_out));
  Button Clr (.out(Clr_out));
  and and_1 (and_1_out, clock_1_out, nand_1_out);
  and and_2 (Pc, decoder_1_out2, or_3_out);
  not not_1 (not_1_out, and_1_out);
  Counter #(.width(4), .max('hf)) counter_1 (
    .load(Pc), .D(register_2_q), .count(InC), .Q(counter_1_q), .clk(and_1_out), .clr(Clr_out));  // open: carry
  Multiplexer #(.width(4), .enable("false")) multiplexer_1 (
    .in0(counter_1_q), .in1(register_2_q), .out(multiplexer_1_out), .sel(Amux));
  and and_3 (Amux, decoder_1_out2, or_2_out);
  Decoder #(.select(2), .enable("false")) decoder_1 (
    .out0(InC), .out1(Ir), .out2(decoder_1_out2), .out3(decoder_1_out3), .sel(counter_2_q));
  Counter #(.width(2), .max('h3)) counter_2 (
    .Q(counter_2_q), .clk(not_1_out), .clr(Clr_out));  // open: load, D, count, carry
  Register #(.width(4)) register_1 (.D(multiplexer_1_out), .en(Mar), .Q(register_1_q), .clk(and_1_out));  // open: clr
  or or_1 (Mar, InC, and_4_out);
  and and_4 (and_4_out, decoder_1_out2, or_2_out);
  or or_2 (or_2_out, and_11_out, and_12_out, and_13_out, and_14_out);
  and and_5 (Mst, decoder_1_out3, and_14_out);
  or or_3 (or_3_out, and_15_out, and_10_out);
  RAM #(.addrWidth(4), .bus("separate")) ram_1 (
    .addr(register_1_q), .din(register_3_q), .data(ram_1_data), .str(Mst), .clk(and_1_out));  // open: sel, ld, clr
  and and_6 (Dmux, decoder_1_out3, and_11_out);
  Multiplexer #(.width(8), .enable("false")) multiplexer_2 (
    .in0(adder_1_out), .in1(ram_1_data), .out(multiplexer_2_out), .sel(Dmux));
  Register register_2 (.D(ram_1_data), .en(Ir), .Q({register_2_q_2, register_2_q}), .clk(and_1_out), .clr(Clr_out));
  and and_7 (Acc, decoder_1_out3, or_4_out);
  or or_4 (or_4_out, and_13_out, and_11_out, and_12_out);
  and and_8 (Sub, decoder_1_out3, and_13_out);
  and and_9 (Out, decoder_1_out3, and_17_out);
  and and_10 (and_10_out, and_18_out, and_16_out);
  Register register_3 (.D(multiplexer_2_out), .en(Acc), .Q(register_3_q), .clk(and_1_out));  // open: clr
  and and_11 (and_11_out, not_2_out[3], not_2_out[2], not_2_out[1], not_2_out[0]);
  and and_12 (and_12_out, not_2_out[3], not_2_out[2], not_2_out[1], register_2_q_2[4]);
  and and_13 (and_13_out, not_2_out[3], not_2_out[2], register_2_q_2[5], not_2_out[0]);
  and and_14 (and_14_out, not_2_out[3], not_2_out[2], register_2_q_2[5], register_2_q_2[4]);
  and and_15 (and_15_out, not_2_out[3], register_2_q_2[6], not_2_out[1], not_2_out[0]);
  and and_16 (and_16_out, not_2_out[3], register_2_q_2[6], not_2_out[1], register_2_q_2[4]);
  and and_17 (and_17_out, register_2_q_2[7], register_2_q_2[6], register_2_q_2[5], not_2_out[0]);
  nand nand_1 (nand_1_out, register_2_q_2[7], register_2_q_2[6], register_2_q_2[5], register_2_q_2[4]);
  Register register_4 (.D(register_3_q), .en(Out), .Q(Output_Display), .clk(and_1_out));  // open: clr
  assign xor_1_out = ram_1_data ^ {8{Sub}};  // XOR_Gate xor_1, 8 bits wide
  assign not_2_out = ~register_2_q_2;  // NOT_Gate not_2, 4 bits wide
  Adder adder_1 (.a(register_3_q), .b(xor_1_out), .out(adder_1_out), .cin(Sub));  // open: cout
  assign not_3_out = ~register_3_q;  // NOT_Gate not_3, 8 bits wide
  and and_18 (and_18_out, not_3_out[7], not_3_out[6], not_3_out[5], not_3_out[4], not_3_out[3], not_3_out[2], not_3_out[1], not_3_out[0]);

  // Notes on the sheet:
  //   PC
  //   MAR
  //   IR
  //   ACC
  //   Lda
  //   Add
  //   Sub
  //   Sta
  //   Jmp
  //   Jaz
  //   Out
  //   Hlt
  //   OUT
endmodule
